# Fritzing sketch polytimeBioPunk (saved by Fritzing 0.8.7b)
circuit board: 3.96993cm x 2.87397cm
breadboards: 1

parts:
  R1 = Resistor [tolerance=±5% resistance=1k package=THT]
  R2 = Resistor [tolerance=±5% resistance=100 package=THT]
  R4 = Photocell (LDR) [package=THT]
  C1 = Capacitor Polarized [package=cpol-radial-100uf-25v]
  J1 = Piezo Speaker
  IC1 = General purpose bipolar Timer [package=dil-08]
  C3 = Capacitor Polarized [package=cpol-radial-100uf-25v]
  U1 = TRANSISTOR_NPN_2 [package=to-92]
  LED1 = LED - 5mm [color="Red (633nm)" package="5 mm [THT]"]
  C4 = Capacitor Polarized [package=cpol-radial-100uf-25v]  # not connected

nets:
  N1: R1.Pin_0, IC1.TRI, IC1.TRE, C3.+
  N2: R1.Pin_1, R4.pin_0, IC1.DIS
  N3: R2.Pin_0, LED1.anode
  N4: R2.Pin_1, R4.pin_1, IC1.VCC+
  N5: C1.+, IC1.OUT
  N6: C1.-, J1.pin1, U1.B
