# Fritzing sketch circuit556 (saved by Fritzing 0.8.7b)
circuit board: 8.46667cm x 5.64444cm
breadboards: 1

parts:
  C1 = Ceramic Capacitor [capacitance=100nF package="100 mil [THT, multilayer]"]
  C2 = Ceramic Capacitor [capacitance=100nF package="100 mil [THT, multilayer]"]
  C3 = Electrolytic Capacitor [capacitance=10µF package="100 mil [THT, electrolytic]"]
  R1 = Resistor [tolerance=±5% resistance=10k package=THT]
  R2 = Resistor [tolerance=±5% resistance=4.7k package=THT]
  R3 = Resistor [tolerance=±5% resistance=1k package=THT]
  U1 = 556 [package=dil14]
  Pad1 = Pad [width=2 height=2 connect=center]
  U3 = POT [package=trim_pot]
  U4 = POT [package=trim_pot]

nets (from the pcb view):
  N1: C1.0, C2.0, U1.GND
  N2: C1.1, R3.Pin_1, U1.DIS, U1.TRIG
  N3: C2.1, U1.DIS2, U3.A
  N4: C3.-, R1.Pin_0
  N5: C3.+, U1.OUT2
  N6: R1.Pin_1, R2.Pin_1, Pad1.pad
  N7: U1.RST, U4.S
  N8: U1.VCC, U3.E, U4.A
