# Fritzing sketch polytime (saved by Fritzing 0.8.7b)
circuit board: 3.06682cm x 3.48074cm
breadboards: 1

parts:
  R1 = Resistor [tolerance=±5% resistance=1k package=THT]
  R2 = Resistor [tolerance=±5% resistance=100 package=THT]
  R3 = Resistor [tolerance=±5% resistance=51 package=THT]
  R4 = Photocell (LDR) [package=THT]
  C1 = Capacitor Polarized [package=cpol-radial-100uf-25v]
  C2 = Capacitor [package=cap-pth-small2]
  J1 = Piezo Speaker
  IC1 = General purpose bipolar Timer [package=dil-08]

nets:
  N1: R1.Pin_0, R4.pin_1, IC1.DIS
  N2: R1.Pin_1, C2.2, IC1._RES, IC1.VCC+
  N3: R2.Pin_0, R4.pin_0
  N4: R2.Pin_1, IC1.TRI
  N5: R3.Pin_0, C1.+
  N6: R3.Pin_1, IC1.OUT
  N7: C1.-, J1.pin1
  N8: C2.1, IC1.TRE
